# Fritzing sketch MotherBoard (saved by Fritzing 0.9.3b)
circuit board: 10cm x 5.64444cm
breadboards: 1

parts:
  J1 = Screw terminal - 2 pins [package=THT]
  J2 = Screw terminal - 2 pins [package=THT]
  J7 = female pin header, 4 pins [form="♀ (female)"]
  J6 = female pin header, 6 pins [form="♀ (female)"]
  J5 = male pin header, 13 pins [form="♂ (male)"]  # not connected
  J4 = male pin header, 13 pins [form="♂ (male)"]

nets:
  VIN-: J1.pin1, J6.pin1
  GND: J1.pin2, J2.pin2, J7.pin4, J6.pin5, J4.pin13
  VIN+: J2.pin1, J6.pin2
  SDA: J7.pin1, J6.pin3, J4.pin11
  SCK: J7.pin2, J6.pin4, J4.pin8
  3.3V: J7.pin3, J6.pin6, J4.pin12
